# Fritzing sketch D7 1 (saved by Fritzing 0.9.3b)

parts:
  Mantık_Seviyesi_Dönüştürücü_5V_-_3_3V = Logic Level Converter [package="Breakout board"]
  R1 = Resistor [tolerance=±5% resistance=4.7k package="2512 [SMD]"]
  R2 = Resistor [tolerance=±5% resistance=4.7k package="2512 [SMD]"]
  Raspberry_Pi_1 = Raspberry Pi 3 [part_number=RPI-3-V1.2]
  BNO055 = 9-DOF Absolute Orientation IMU Fusion Breakout - BNO055  # not connected
  M1 = Stepper Motor - Bipolar
  M2 = Stepper Motor - Bipolar
  M3 = Stepper Motor - Bipolar
  A4988 = Pololu A4988 [package=SO16]
  A4988_2 = Pololu A4988 [package=SO16]
  A4988_3 = Pololu A4988 [package=SO16]
  Motor_Power_Supply = Power plug
  100uF = Capacitor Polarized [package=cpol-radial-100uf-25v]  # not connected
  Basınç_Sensörü = Barometric Pressure Sensor - BMP180 Breakout (GY-68)
  Parça2 = Arduino Mega 2560 (Rev3)
  5V = Power plug
  U1 = SUP500F [package=sup500f]

nets:
  3V3: Mantık_Seviyesi_Dönüştürücü_5V_-_3_3V.LV, Raspberry_Pi_1.3v3, Basınç_Sensörü.VCC
  GND: Mantık_Seviyesi_Dönüştürücü_5V_-_3_3V.L-GND, Raspberry_Pi_1.GND, Raspberry_Pi_1.GIPO13, Raspberry_Pi_1.GIPO16, Basınç_Sensörü.GND, Parça2.GND, 5V.GND, U1.GND
  N1: Mantık_Seviyesi_Dönüştürücü_5V_-_3_3V.LV3, Raspberry_Pi_1.GIPO14
  N2: Mantık_Seviyesi_Dönüştürücü_5V_-_3_3V.LV4, Raspberry_Pi_1.GIPO15
  N3: Mantık_Seviyesi_Dönüştürücü_5V_-_3_3V.HV4, Parça2.D1_TX0
  N4: Mantık_Seviyesi_Dönüştürücü_5V_-_3_3V.HV3, Parça2.D0_RX0
  N5: R1.Pin_0, Parça2.D20/SDA
  N6: R2.Pin_0, Parça2.D21/SCL
  N7: Raspberry_Pi_1.GPIO2, Basınç_Sensörü.SDA
  N8: Raspberry_Pi_1.GPIO3, Raspberry_Pi_1.GIPO4, Basınç_Sensörü.SCL
  N9: Raspberry_Pi_1.GIPO24, U1.TX-O
  N10: Raspberry_Pi_1.GIPO23, U1.RX-I
  N11: M1.A, A4988.2B
  N12: M1.C, A4988.2A
  N13: M1.B, A4988.1A
  N14: M1.D, A4988.1B
  N15: M2.A, A4988_2.2B
  N16: M2.C, A4988_2.2A
  N17: M2.B, A4988_2.1A
  N18: M2.D, A4988_2.1B
  N19: M3.A, A4988_3.2B
  N20: M3.C, A4988_3.2A
  N21: M3.B, A4988_3.1A
  N22: M3.D, A4988_3.1B
  N23: A4988.ENABLE, Parça2.D31
  N24: A4988.RESET, A4988.SLEEP
  N25: A4988.STEP, Parça2.D33
  N26: A4988.DIR, Parça2.D35
  N27: A4988.VMOT, Motor_Power_Supply.VCC
  N28: A4988_2.ENABLE, Parça2.D37
  N29: A4988_2.RESET, A4988_2.SLEEP
  N30: A4988_2.STEP, Parça2.D39
  N31: A4988_2.DIR, Parça2.D41
  N32: A4988_3.ENABLE, Parça2.D43
  N33: A4988_3.RESET, A4988_3.SLEEP
  N34: A4988_3.STEP, Parça2.D45
  N35: A4988_3.DIR, Parça2.D47
  VIN: Parça2.VIN, 5V.VCC

custom parts:
  Logic Level Converter: 5V to/from 3.3V logic level converter
  9-DOF Absolute Orientation IMU Fusion Breakout - BNO055: A MEMS accelerometer, magnetometer and gyroscope on a single die with a high speed ARM Cortex-M0 based processor to digest all the sensor data, abstract the sensor fusion and real time requirements away, and spit out data you can use in quaternions, Euler angles or vectors.
