# Fritzing sketch D7 2 (saved by Fritzing 0.9.3b)

parts:
  Mantık_Seviyesi_Dönüştürücü_5V_-_3_3V = Logic Level Converter [package="Breakout board"]
  R1 = Resistor [tolerance=±5% resistance=4.7k package="2512 [SMD]"]
  R2 = Resistor [tolerance=±5% resistance=4.7k package="2512 [SMD]"]
  Raspberry_Pi_1 = Raspberry Pi 3 [part_number=RPI-3-V1.2]
  BNO055 = 9-DOF Absolute Orientation IMU Fusion Breakout - BNO055  # not connected
  M1 = Stepper Motor - Bipolar
  M2 = Stepper Motor - Bipolar
  M3 = Stepper Motor - Bipolar
  A4988 = Pololu A4988 [package=SO16]
  A4988_2 = Pololu A4988 [package=SO16]
  A4988_3 = Pololu A4988 [package=SO16]
  Motor_Power_Supply = Power plug
  100uF = Capacitor Polarized [package=cpol-radial-100uf-25v]  # not connected
  Basınç_Sensörü = Barometric Pressure Sensor - BMP180 Breakout (GY-68)
  Parça2 = Arduino Mega 2560 (Rev3)
  5V = Power plug
  MCP2515_CAN = Niren can bus module [package=THT]
  MCP2515_CAN_2 = Niren can bus module [package=THT]
  GPS = SUP500F [package=sup500f]

nets:
  N1: Mantık_Seviyesi_Dönüştürücü_5V_-_3_3V.LV1, Raspberry_Pi_1.GIPO11
  N2: Mantık_Seviyesi_Dönüştürücü_5V_-_3_3V.LV2, Raspberry_Pi_1.GIPO10
  N3: Mantık_Seviyesi_Dönüştürücü_5V_-_3_3V.LV, Raspberry_Pi_1.3v3, Basınç_Sensörü.SCL
  GND: Mantık_Seviyesi_Dönüştürücü_5V_-_3_3V.L-GND, Raspberry_Pi_1.GND, Basınç_Sensörü.SDA, Parça2.GND, 5V.GND, GPS.GND
  N4: Mantık_Seviyesi_Dönüştürücü_5V_-_3_3V.LV3, Raspberry_Pi_1.GIPO9
  N5: Mantık_Seviyesi_Dönüştürücü_5V_-_3_3V.LV4, Raspberry_Pi_1.GIPO8
  N6: Mantık_Seviyesi_Dönüştürücü_5V_-_3_3V.HV4, MCP2515_CAN.pin3
  N7: Mantık_Seviyesi_Dönüştürücü_5V_-_3_3V.HV3, MCP2515_CAN.pin4
  N8: Mantık_Seviyesi_Dönüştürücü_5V_-_3_3V.HV2, MCP2515_CAN.pin5
  N9: Mantık_Seviyesi_Dönüştürücü_5V_-_3_3V.HV1, MCP2515_CAN.pin6
  N10: R1.Pin_0, Parça2.D20/SDA
  N11: R2.Pin_0, Parça2.D21/SCL
  N12: Raspberry_Pi_1.GPIO2, Basınç_Sensörü.VCC
  N13: Raspberry_Pi_1.GPIO3, Basınç_Sensörü.GND
  N14: Raspberry_Pi_1.GIPO15, GPS.TX-O
  N15: Raspberry_Pi_1.GIPO14, GPS.RX-I
  N16: M1.A, A4988.2B
  N17: M1.C, A4988.2A
  N18: M1.B, A4988.1A
  N19: M1.D, A4988.1B
  N20: M2.A, A4988_2.2B
  N21: M2.C, A4988_2.2A
  N22: M2.B, A4988_2.1A
  N23: M2.D, A4988_2.1B
  N24: M3.A, A4988_3.2B
  N25: M3.C, A4988_3.2A
  N26: M3.B, A4988_3.1A
  N27: M3.D, A4988_3.1B
  N28: A4988.ENABLE, Parça2.D31
  N29: A4988.RESET, A4988.SLEEP
  N30: A4988.STEP, Parça2.D33
  N31: A4988.DIR, Parça2.D35
  N32: A4988.VMOT, Motor_Power_Supply.VCC
  N33: A4988_2.ENABLE, Parça2.D37
  N34: A4988_2.RESET, A4988_2.SLEEP
  N35: A4988_2.STEP, Parça2.D39
  N36: A4988_2.DIR, Parça2.D41
  N37: A4988_3.ENABLE, Parça2.D43
  N38: A4988_3.RESET, A4988_3.SLEEP
  N39: A4988_3.STEP, Parça2.D45
  N40: A4988_3.DIR, Parça2.D47
  VIN: Parça2.VIN, 5V.VCC
  N41: Parça2.D2_PWM, MCP2515_CAN_2.pin7
  N42: Parça2.D50, MCP2515_CAN_2.pin4
  N43: Parça2.D51, MCP2515_CAN_2.pin5
  N44: Parça2.D52, MCP2515_CAN_2.pin6
  N45: Parça2.D53, MCP2515_CAN_2.pin3
  N46: MCP2515_CAN.pin12, MCP2515_CAN_2.pin10, MCP2515_CAN_2.pin12
  N47: MCP2515_CAN.pin13, MCP2515_CAN_2.pin11, MCP2515_CAN_2.pin13

custom parts:
  Logic Level Converter: 5V to/from 3.3V logic level converter
  9-DOF Absolute Orientation IMU Fusion Breakout - BNO055: A MEMS accelerometer, magnetometer and gyroscope on a single die with a high speed ARM Cortex-M0 based processor to digest all the sensor data, abstract the sensor fusion and real time requirements away, and spit out data you can use in quaternions, Euler angles or vectors.
  Niren can bus module: Niren can bus module availabe on ebay and others. No pcb view as no mechanical drawng and it wouldn't mount anyway.
