# Fritzing sketch D7 3 (saved by Fritzing 0.9.3b)

parts:
  Mantık_Seviyesi_Dönüştürücü_5V_-_3_3V = Logic Level Converter [package="Breakout board"]
  R1 = Resistor [tolerance=±5% resistance=4.7k package="2512 [SMD]"]
  R2 = Resistor [tolerance=±5% resistance=4.7k package="2512 [SMD]"]
  BNO055 = 9-DOF Absolute Orientation IMU Fusion Breakout - BNO055  # not connected
  M1 = Stepper Motor - Bipolar
  M2 = Stepper Motor - Bipolar
  M3 = Stepper Motor - Bipolar
  A4988 = Pololu A4988 [package=SO16]
  A4988_2 = Pololu A4988 [package=SO16]
  A4988_3 = Pololu A4988 [package=SO16]
  Motor_Power_Supply = Power plug
  100uF = Capacitor Polarized [package=cpol-radial-100uf-25v]  # not connected
  Basınç_Sensörü = Barometric Pressure Sensor - BMP180 Breakout (GY-68)
  Parça2 = Arduino Mega 2560 (Rev3)
  5V = Power plug
  GPS = SUP500F [package=sup500f]
  3_3V = Power plug

nets:
  N1: Mantık_Seviyesi_Dönüştürücü_5V_-_3_3V.LV1, Basınç_Sensörü.SDA
  N2: Mantık_Seviyesi_Dönüştürücü_5V_-_3_3V.LV2, Basınç_Sensörü.SCL
  N3: Mantık_Seviyesi_Dönüştürücü_5V_-_3_3V.LV, 3_3V.VCC
  N4: Mantık_Seviyesi_Dönüştürücü_5V_-_3_3V.L-GND, 3_3V.GND
  N5: R1.Pin_0, Parça2.D20/SDA
  N6: R2.Pin_0, Parça2.D21/SCL
  N7: M1.A, A4988.2B
  N8: M1.C, A4988.2A
  N9: M1.B, A4988.1A
  N10: M1.D, A4988.1B
  N11: M2.A, A4988_2.2B
  N12: M2.C, A4988_2.2A
  N13: M2.B, A4988_2.1A
  N14: M2.D, A4988_2.1B
  N15: M3.A, A4988_3.2B
  N16: M3.C, A4988_3.2A
  N17: M3.B, A4988_3.1A
  N18: M3.D, A4988_3.1B
  N19: A4988.ENABLE, Parça2.D31
  N20: A4988.RESET, A4988.SLEEP
  N21: A4988.STEP, Parça2.D33
  N22: A4988.DIR, Parça2.D35
  N23: A4988.VMOT, Motor_Power_Supply.VCC
  N24: A4988_2.ENABLE, Parça2.D37
  N25: A4988_2.RESET, A4988_2.SLEEP
  N26: A4988_2.STEP, Parça2.D39
  N27: A4988_2.DIR, Parça2.D41
  N28: A4988_3.ENABLE, Parça2.D43
  N29: A4988_3.RESET, A4988_3.SLEEP
  N30: A4988_3.STEP, Parça2.D45
  N31: A4988_3.DIR, Parça2.D47
  GND: Parça2.GND, 5V.GND
  VIN: Parça2.VIN, 5V.VCC
  N32: Parça2.D0_RX0, GPS.TX-O
  N33: Parça2.D1_TX0, GPS.RX-I

custom parts:
  Logic Level Converter: 5V to/from 3.3V logic level converter
  9-DOF Absolute Orientation IMU Fusion Breakout - BNO055: A MEMS accelerometer, magnetometer and gyroscope on a single die with a high speed ARM Cortex-M0 based processor to digest all the sensor data, abstract the sensor fusion and real time requirements away, and spit out data you can use in quaternions, Euler angles or vectors.
